# Fritzing sketch unijoysticle (saved by Fritzing 0.9.2b)
circuit board: 10cm x 6cm
breadboards: 1

parts:
  U1 = NodeMCU V1.0
  74HC1 = DIP - 14 pins [chip_label=4066 package="DIP (Dual Inline) [THT]"]
  74HC2 = DIP - 14 pins [chip_label=4066 package="DIP (Dual Inline) [THT]"]
  X2 = DB9 Connector [package=db9]

nets:
  VCC: U1.3V3, 74HC1.Vcc, 74HC2.Vcc
  N1: U1.D6, 74HC2.1C
  N2: U1.D7, 74HC1.4C
  N3: U1.D8, U1.RX, 74HC1.1B, 74HC1.2C, 74HC1.3B, 74HC1.4B, 74HC2.1B, X2.3
  N4: U1.TX, 74HC1.1C
  GND: U1.GND, 74HC1.GND, 74HC2.GND
  N5: 74HC1.1A, X2.1
  N6: 74HC1.2A, X2.7
  N7: 74HC1.3A, X2.6
  N8: 74HC1.4A, X2.8
  N9: 74HC2.1A, X2.9

notes:
  Uni-Joysti-Cle™ WiFi receiver v0.1

custom parts:
  NodeMCU V1.0: ESP9266 based NodeMCU
  DIP - 14 pins: Quadruple bilateral analog switch
